# Fritzing sketch zuim-clock-schematic (saved by Fritzing 0.9.6b)
breadboards: 1

parts:
  MH-ET_LIVE_ESP32_DEVKIT1 = MH-ET LIVE ESP32 DEVKIT 38 pins
  OLED1 = 128x64 Monochrom OLED Display with SPI Control
  S1 = Pushbutton [package="[THT]"]
  S2 = Pushbutton [package="[THT]"]
  S3 = Pushbutton [package="[THT]"]
  S4 = Pushbutton [package="[THT]"]
  S5 = Pushbutton [package="[THT]"]
  R1 = Resistor [tolerance=±5% resistance=330 package="1206 [SMD]"]
  LED1 = smd LED [color="Red (633nm)" package="0603 [SMD]"]
  R2 = Resistor [tolerance=±5% resistance=1k package="1206 [SMD]"]
  R3 = Resistor [tolerance=±5% resistance=1k package="1206 [SMD]"]
  R4 = Resistor [tolerance=±5% resistance=1k package="1206 [SMD]"]
  R5 = Resistor [tolerance=±5% resistance=1k package="1206 [SMD]"]
  R6 = Resistor [tolerance=±5% resistance=1k package="1206 [SMD]"]

nets:
  3V3: MH-ET_LIVE_ESP32_DEVKIT1.3V3, MH-ET_LIVE_ESP32_DEVKIT1.IO16, OLED1.Vin, S1.Pin_3, S1.Pin_4, S2.Pin_1, S2.Pin_2, S3.Pin_1, S3.Pin_2, S4.Pin_1, S4.Pin_2, S5.Pin_1, S5.Pin_2
  N1: MH-ET_LIVE_ESP32_DEVKIT1.IO25, LED1.anode
  N2: MH-ET_LIVE_ESP32_DEVKIT1.IO26, OLED1.Reset
  N3: MH-ET_LIVE_ESP32_DEVKIT1.IO27, OLED1.SA0/DC
  N4: MH-ET_LIVE_ESP32_DEVKIT1.IO14, OLED1.Clock
  N5: MH-ET_LIVE_ESP32_DEVKIT1.IO13, OLED1.Data
  GND: MH-ET_LIVE_ESP32_DEVKIT1.GND, OLED1.GND, R1.Pin_1, R2.Pin_1, R3.Pin_1, R4.Pin_1, R5.Pin_1, R6.Pin_1
  N6: MH-ET_LIVE_ESP32_DEVKIT1.IO19, S5.Pin_3, S5.Pin_4, R2.Pin_0
  N7: MH-ET_LIVE_ESP32_DEVKIT1.IO18, S4.Pin_3, S4.Pin_4, R3.Pin_0
  N8: MH-ET_LIVE_ESP32_DEVKIT1.IO5, S3.Pin_3, S3.Pin_4, R4.Pin_0
  N9: MH-ET_LIVE_ESP32_DEVKIT1.IO17, S2.Pin_3, S2.Pin_4, R5.Pin_0
  N10: MH-ET_LIVE_ESP32_DEVKIT1.IO15, OLED1.CS
  N11: S1.Pin_1, S1.Pin_2, R6.Pin_0
  N12: R1.Pin_0, LED1.cathode

custom parts:
  MH-ET LIVE ESP32 DEVKIT 38 pins: http://mh.nodebb.com/topic/2/mh-et-live-esp32-devkit
